// Logisim project HW5Q1.circ as structural Verilog: 1 circuit, main circuit main
module main (
  input  X,
  input  Y,
  input  Z,
  output SUM,
  output Carry_OUT
);

  wire and_1_out, and_2_out, xor_1_out;

  xor xor_1 (xor_1_out, X, Y);
  xor xor_2 (SUM, xor_1_out, Z);
  and and_1 (and_1_out, Z, xor_1_out);
  and and_2 (and_2_out, Y, X);
  or or_1 (Carry_OUT, and_1_out, and_2_out);

  // Notes on the sheet:
  //   FULL ADDER
endmodule
