// Logisim project HW5Q2.circ as structural Verilog: 1 circuit, main circuit main
module main (
  input  x,
  input  y,
  output S,
  output Q,
  output Carry_out
);

  wire adder_1_cout, clock_out;

  Adder #(.width(1)) adder_1 (.a(x), .b(y), .out(S), .cin(Q), .cout(adder_1_cout));
  not not_1 (Carry_out, adder_1_cout);
  Clock clock (.out(clock_out));
  D_Flip_Flop d_ff_1 (.clk(clock_out), .D(Carry_out), .Q(Q));  // open: Qn, preset, en, reset

  // Notes on the sheet:
  //   Carry in
  //   Sum
endmodule
