// Logisim project HW5Q3.circ as structural Verilog: 1 circuit, main circuit main
module main (
  input  x,
  input  y,
  output Z
);

  wire A_q, clock_1_out, j_k_ff_1_q, not_1_out, not_2_out, nxy_out, nyB__xy_out, nyB_out, xB_nyA_out, xB_out,
       xy_out, yB_nxy_out, yB_out;

  not not_1 (not_1_out, x);
  not not_2 (not_2_out, y);
  and yB (yB_out, y, j_k_ff_1_q);
  and nxy (nxy_out, y, not_1_out);
  and nyB (nyB_out, j_k_ff_1_q, not_2_out);
  and xy (xy_out, y, x);
  // AND_Gate nyA has open pins: in1=not_2_out, in4=A_q, out=open
  and xB (xB_out, x, j_k_ff_1_q);
  or or_1 (Z, nxy_out, x);
  Clock clock_1 (.out(clock_1_out));
  or yB_nxy (yB_nxy_out, yB_out, nxy_out);
  or nyB__xy (nyB__xy_out, nyB_out, xy_out);
  or xB_nyA (xB_nyA_out, xy_out, xB_out);
  D_Flip_Flop A (.clk(clock_1_out), .D(yB_nxy_out), .Q(A_q));  // open: Qn, preset, en, reset
  J_K_Flip_Flop j_k_ff_1 (
    .J(nyB__xy_out), .clk(clock_1_out), .K(xB_nyA_out), .Q(j_k_ff_1_q));  // open: Qn, preset, en, reset
endmodule
