// Logisim project HW5Q4.circ as structural Verilog: 1 circuit, main circuit main
module main (
  output A,
  output B,
  output C
);

  wire A_qn, AB_out, B_C_out, B_qn, C_qn, clock_1_out, nA_nB_out, nA_nC_out, nB_nC_out, or_1_out;

  or nA_nC (nA_nC_out, A_qn, C_qn);
  and nA_nB (nA_nB_out, A_qn, B_qn);
  and AB (AB_out, A, B);
  or nB_nC (nB_nC_out, B, C_qn);
  or B_C (B_C_out, B, C);
  or or_1 (or_1_out, nA_nB_out, AB_out);
  Clock clock_1 (.out(clock_1_out));
  J_K_Flip_Flop u_A (.J(nB_nC_out), .clk(clock_1_out), .K(B_C_out), .Q(A), .Qn(A_qn));  // open: preset, en, reset
  J_K_Flip_Flop u_B (.J(nA_nC_out), .clk(clock_1_out), .K(nA_nC_out), .Q(B), .Qn(B_qn));  // open: preset, en, reset
  J_K_Flip_Flop u_C (.J(or_1_out), .clk(clock_1_out), .K(A), .Q(C), .Qn(C_qn));  // open: preset, en, reset
endmodule
